// Digital circuit Ctrl_ULA.dig as structural Verilog
module Ctrl_ULA (
  input  [1:0] Op_ULA,
  input  [2:0] Func,
  output Ain,
  output Bin,
  output Cin,
  output [1:0] ControleULA
);

  wire and_1_out, and_2_out, and_3_out, and_4_out, and_5_out, and_7_out, not_1_out, not_2_out, not_3_out,
       not_4_out, not_5_out;

  not not_1 (not_1_out, Func[1]);
  not not_2 (not_2_out, Func[2]);
  not not_3 (not_3_out, Op_ULA[1]);
  not not_4 (not_4_out, Func[0]);
  not not_5 (not_5_out, Op_ULA[0]);
  and and_1 (and_1_out, not_4_out, not_1_out, Func[2], not_5_out);
  and and_2 (and_2_out, not_5_out, Func[2]);
  or or_1 (ControleULA[0], Op_ULA[0], Op_ULA[1], not_1_out);
  and and_3 (and_3_out, not_5_out, not_3_out, not_4_out, Func[1], Func[2]);
  and and_4 (and_4_out, not_5_out, not_3_out, Func[0], not_2_out);
  and and_5 (and_5_out, not_5_out, not_3_out, Func[0], not_1_out);
  and and_6 (Ain, not_5_out, not_3_out, Func[0], Func[1]);
  and and_7 (and_7_out, Func[0], Func[1], not_5_out);
  or or_2 (Cin, and_2_out, Op_ULA[1]);
  or or_3 (Bin, and_1_out, Op_ULA[1], and_7_out);
  or or_4 (ControleULA[1], and_3_out, and_4_out, and_5_out);

  // Notes on the sheet:
  //   Ain = ~C0*~C1*F0*F1
  //   Bin = ~F0*~F1*F2*~C0 + F0*F1*~C0 + C1
  //   Cin = C1 + ~C0*F2
  //   Op_0 = C1+C0+~F1
  //   Op_1 = ~C0*~C1*~F0*F1*F2 + ~C0*~C1*F0*~F2 + ~C0*~C1*F0*~F1
  //   F2, F1, F0, C1, C0
  //   Negado, Normal
  //   ~F2
  //   F2
  //   ~F1
  //   F1
  //   ~F0
  //   F0
  //   ~C1
  //   C1
  //   ~C0
  //   C0
endmodule
